// Logisim project processeur.circ as structural Verilog: 14 circuits, main circuit main
module main (
  input  in_1
);

  wire alu_4_bits_1_rs_subs, clk_out, controleur_1_add, controleur_1_and, controleur_1_fetch,
       controleur_1_not, controleur_1_or, controleur_1_read, controleur_1_subs, controleur_1_wad,
       controleur_1_wpc, controleur_1_write, not_1_out, not_2_out, not_3_out;
  wire [1:0] controleur_1_res, controleur_1_x, controleur_1_y;
  wire [3:0] alu_4_bits_1_res, banc_de_registres_1_xi, banc_de_registres_1_yi, or_1_out, pc_1_p8,
       pull_resistor_3_node, select_1_s, select_2_s, select_3_s, select_4_s;
  wire [5:0] ad_1_r_2, controleur_1_imme;
  wire [11:0] registre_d_instructions_1_xi, rom_1_data;

  Clock clk (.out(clk_out));
  Registre_d_instructions registre_d_instructions_1 (
    .R(rom_1_data), .Xi(registre_d_instructions_1_xi), .clk(clk_out), .Winstrct(1'b1), .Reset(1'b0),
    .Enable(1'b1), .Preset(1'b0), .selXi(1'b1));
  assign or_1_out = select_1_s | select_2_s;  // OR_Gate or_1, 4 bits wide
  Banc_de_registres banc_de_registres_1 (
    .Reset(1'b0), .Enable(1'b1), .Preset(1'b0), .clk(clk_out), .selRi(controleur_1_res), .R(or_1_out),
    .selXi(controleur_1_x), .selYi(controleur_1_y), .Xi(banc_de_registres_1_xi), .Yi(banc_de_registres_1_yi));
  Select select_1 (.R(alu_4_bits_1_res), .enable(not_1_out), .S(select_1_s));
  Select select_2 (.R(pull_resistor_3_node), .enable(controleur_1_read), .S(select_2_s));
  Pull_Resistor pull_resistor_1 (.node(select_1_s));
  Pull_Resistor pull_resistor_2 (.node(select_2_s));
  Select select_3 (.R(banc_de_registres_1_xi), .enable(not_2_out), .S(select_3_s));
  LED led_1 (.in(alu_4_bits_1_rs_subs));
  not not_1 (not_1_out, controleur_1_read);
  ALU_4_bits alu_4_bits_1 (
    .Re(1'b0), .A(select_4_s), .B(select_3_s), .AND(controleur_1_and), .OR(controleur_1_or),
    .nB(controleur_1_not), .ADD(controleur_1_add), .Res(alu_4_bits_1_res), .SUBS(controleur_1_subs),
    .Rs_subs(alu_4_bits_1_rs_subs));  // open: Rs
  Select select_4 (.R(banc_de_registres_1_yi), .enable(not_2_out), .S(select_4_s));
  not not_2 (not_2_out, controleur_1_write);
  Controleur controleur_1 (
    .Instruct_In(registre_d_instructions_1_xi), .ADD(controleur_1_add), .OR(controleur_1_or),
    .AND(controleur_1_and), .NOT(controleur_1_not), .X(controleur_1_x), .Y(controleur_1_y),
    .Res(controleur_1_res), .clk(clk_out), .wPC(controleur_1_wpc), .wAD(controleur_1_wad),
    .Fetch(controleur_1_fetch), .Write(controleur_1_write), .Read(controleur_1_read),
    .Imme(controleur_1_imme), .SUBS(controleur_1_subs));  // open: LOAD, STORE
  AD ad_1 (
    .R(controleur_1_imme), .R_2(ad_1_r_2), .clk(clk_out), .Wa(controleur_1_wad), .Reset(1'b0), .Enable(1'b1),
    .Preset(1'b0));
  // PC pc_1: pin names not known; wires that end beside it: clk_out, controleur_1_wpc, 1'b1, controleur_1_fetch, in_1, 1'b1, 1'b0, pc_1_p8
  Pull_Resistor pull_resistor_3 (.node(pull_resistor_3_node));
  assign pull_resistor_3_node = controleur_1_write ? banc_de_registres_1_xi : 4'bz;  // Controlled_Buffer controlled_buffer_1
  not not_3 (not_3_out, controleur_1_write);
  ROM #(.addrWidth(4), .dataWidth(12)) rom_1 (.addr(pc_1_p8), .data(rom_1_data));  // open: sel
  RAM #(.addrWidth(6), .dataWidth(4), .bus("separate")) ram_1 (
    .addr(ad_1_r_2), .din(pull_resistor_3_node), .data(pull_resistor_3_node), .clk(clk_out), .ld(not_3_out));  // open: str, sel, clr

  // Notes on the sheet:
  //   contents of rom_1 (hex, n*v repeats v):
  //   0 4c1 482 96c 843
endmodule

module Full_Adder (
  input  A,
  input  B,
  input  Re,
  output Rs,
  output S
);

  wire and_1_out, and_2_out, and_3_out, xor_1_out;

  and and_1 (and_1_out, A, Re);
  and and_2 (and_2_out, B, Re);
  and and_3 (and_3_out, B, A);
  or or_1 (Rs, and_1_out, and_2_out, and_3_out);
  xor xor_1 (xor_1_out, Re, B);
  xor xor_2 (S, xor_1_out, A);
endmodule

module ALU (
  input  A,
  input  B,
  input  Re,
  input  Re_subs,
  input  AND,
  input  OR,
  input  nB,
  input  ADD,
  input  SUBS,
  output S,
  output Rs,
  output Rs_subs
);

  wire and_1_out, and_2_out, and_3_out, and_4_out, and_5_out, and_6_out, full_adder_1_s, not_1_out, or_1_out,
       substractor_1_s;

  Pull_Resistor pull_resistor_1 (.node(A));
  Pull_Resistor pull_resistor_2 (.node(B));
  and and_1 (and_1_out, A, B);
  or or_1 (or_1_out, A, B);
  not not_1 (not_1_out, B);
  Full_Adder full_adder_1 (.Rs(Rs), .A(A), .B(Re), .Re(B), .S(full_adder_1_s));
  Substractor substractor_1 (.Rs(Rs_subs), .S(substractor_1_s), .A(A), .B(B), .Re(Re_subs));
  and and_2 (and_2_out, SUBS, substractor_1_s);
  and and_3 (and_3_out, AND, and_1_out);
  and and_4 (and_4_out, OR, or_1_out);
  and and_5 (and_5_out, nB, not_1_out);
  and and_6 (and_6_out, ADD, full_adder_1_s);
  or or_2 (S, and_3_out, and_4_out, and_2_out, and_5_out, and_6_out);
endmodule

module Registre_4_bits (
  input  clk,
  input  [3:0] R,
  input  rXi,
  input  rYi,
  input  Wa,
  input  Reset,
  input  Enable,
  input  Preset,
  output [3:0] Yi,
  output [3:0] Xi
);

  wire controlled_buffer_1_out, controlled_buffer_2_out, controlled_buffer_3_out, controlled_buffer_4_out,
       d_ff_1_q, d_ff_2_q, d_ff_3_q, d_ff_4_q;

  assign controlled_buffer_1_out = Wa ? R[0] : 1'bz;  // Controlled_Buffer controlled_buffer_1
  assign controlled_buffer_2_out = Wa ? R[1] : 1'bz;  // Controlled_Buffer controlled_buffer_2
  assign controlled_buffer_3_out = Wa ? R[2] : 1'bz;  // Controlled_Buffer controlled_buffer_3
  assign controlled_buffer_4_out = Wa ? R[3] : 1'bz;  // Controlled_Buffer controlled_buffer_4
  D_Flip_Flop d_ff_1 (
    .clk(clk), .D(controlled_buffer_1_out), .Q(d_ff_1_q), .preset(Preset), .en(Enable), .reset(Reset));  // open: Qn
  D_Flip_Flop d_ff_2 (
    .clk(clk), .D(controlled_buffer_2_out), .Q(d_ff_2_q), .preset(Preset), .en(Enable), .reset(Reset));  // open: Qn
  D_Flip_Flop d_ff_3 (
    .clk(clk), .D(controlled_buffer_3_out), .Q(d_ff_3_q), .preset(Preset), .en(Enable), .reset(Reset));  // open: Qn
  D_Flip_Flop d_ff_4 (
    .clk(clk), .D(controlled_buffer_4_out), .Q(d_ff_4_q), .preset(Preset), .en(Enable), .reset(Reset));  // open: Qn
  assign Xi[0] = rXi ? d_ff_1_q : 1'bz;  // Controlled_Buffer controlled_buffer_5
  assign Xi[1] = rXi ? d_ff_2_q : 1'bz;  // Controlled_Buffer controlled_buffer_6
  assign Xi[2] = rXi ? d_ff_3_q : 1'bz;  // Controlled_Buffer controlled_buffer_7
  assign Yi[0] = rYi ? d_ff_1_q : 1'bz;  // Controlled_Buffer controlled_buffer_8
  assign Xi[3] = rXi ? d_ff_4_q : 1'bz;  // Controlled_Buffer controlled_buffer_9
  assign Yi[1] = rYi ? d_ff_2_q : 1'bz;  // Controlled_Buffer controlled_buffer_10
  assign Yi[2] = rYi ? d_ff_3_q : 1'bz;  // Controlled_Buffer controlled_buffer_11
  assign Yi[3] = rYi ? d_ff_4_q : 1'bz;  // Controlled_Buffer controlled_buffer_12
endmodule

module Select (
  input  [3:0] R,
  input  enable,
  output [3:0] S
);

  assign S[3] = enable ? R[3] : 1'bz;  // Controlled_Buffer controlled_buffer_1
  assign S[0] = enable ? R[0] : 1'bz;  // Controlled_Buffer controlled_buffer_2
  assign S[1] = enable ? R[1] : 1'bz;  // Controlled_Buffer controlled_buffer_3
  assign S[2] = enable ? R[2] : 1'bz;  // Controlled_Buffer controlled_buffer_4
endmodule

module Banc_de_registres (
  input  Reset,
  input  Enable,
  input  Preset,
  input  clk,
  input  [1:0] selRi,
  input  [3:0] R,
  input  [1:0] selXi,
  input  [1:0] selYi,
  output [3:0] Xi,
  output [3:0] Yi
);

  wire and_1_out, and_2_out, and_3_out, and_4_out, and_5_out, and_6_out, and_7_out, and_8_out, and_9_out,
       and_10_out, and_11_out, and_12_out, not_1_out;
  wire [3:0] registre_4_bits_1_xi, registre_4_bits_1_yi, registre_4_bits_2_xi, registre_4_bits_2_yi,
       registre_4_bits_3_xi, registre_4_bits_3_yi, registre_4_bits_4_xi, registre_4_bits_4_yi, select_1_s,
       select_2_s, select_3_s, select_4_s, select_5_s, select_6_s, select_7_s, select_8_s, select_9_s,
       select_10_s, select_11_s, select_12_s;

  and and_1 (and_1_out, ~selRi[0], ~selRi[1]);  // AND_Gate
  and and_2 (and_2_out, ~selRi[0], selRi[1]);  // AND_Gate
  and and_3 (and_3_out, selRi[0], ~selRi[1]);  // AND_Gate
  and and_4 (and_4_out, selRi[0], selRi[1]);
  and and_5 (and_5_out, ~selXi[0], ~selXi[1]);  // AND_Gate
  and and_6 (and_6_out, ~selXi[0], selXi[1]);  // AND_Gate
  and and_7 (and_7_out, selXi[0], ~selXi[1]);  // AND_Gate
  and and_8 (and_8_out, selXi[0], selXi[1]);
  and and_9 (and_9_out, ~selYi[0], ~selYi[1]);  // AND_Gate
  and and_10 (and_10_out, ~selYi[0], selYi[1]);  // AND_Gate
  and and_11 (and_11_out, selYi[0], ~selYi[1]);  // AND_Gate
  and and_12 (and_12_out, selYi[0], selYi[1]);
  not not_1 (not_1_out, clk);
  Select select_1 (.R(R), .enable(and_1_out), .S(select_1_s));
  Select select_2 (.R(R), .enable(and_2_out), .S(select_2_s));
  Select select_3 (.R(R), .enable(and_3_out), .S(select_3_s));
  Select select_4 (.R(R), .enable(and_4_out), .S(select_4_s));
  Registre_4_bits registre_4_bits_1 (
    .Yi(registre_4_bits_1_yi), .Xi(registre_4_bits_1_xi), .R(select_1_s), .Wa(and_1_out), .Reset(Reset),
    .Preset(Preset), .rXi(and_5_out), .rYi(and_9_out), .clk(not_1_out), .Enable(Enable));
  Select select_5 (.R(registre_4_bits_1_xi), .enable(and_5_out), .S(select_5_s));
  Select select_6 (.R(registre_4_bits_1_yi), .enable(and_9_out), .S(select_6_s));
  Registre_4_bits registre_4_bits_2 (
    .Yi(registre_4_bits_2_yi), .Xi(registre_4_bits_2_xi), .R(select_2_s), .Wa(and_2_out), .Reset(Reset),
    .Preset(Preset), .rXi(and_6_out), .rYi(and_10_out), .clk(not_1_out), .Enable(Enable));
  Select select_7 (.R(registre_4_bits_2_xi), .enable(and_6_out), .S(select_7_s));
  Select select_8 (.R(registre_4_bits_2_yi), .enable(and_10_out), .S(select_8_s));
  Registre_4_bits registre_4_bits_3 (
    .Yi(registre_4_bits_3_yi), .Xi(registre_4_bits_3_xi), .R(select_3_s), .Wa(and_3_out), .Reset(Reset),
    .Preset(Preset), .rXi(and_7_out), .rYi(and_11_out), .clk(not_1_out), .Enable(Enable));
  Select select_9 (.R(registre_4_bits_3_xi), .enable(and_7_out), .S(select_9_s));
  Select select_10 (.R(registre_4_bits_3_yi), .enable(and_11_out), .S(select_10_s));
  Select select_11 (.R(registre_4_bits_4_yi), .enable(and_12_out), .S(select_11_s));
  Registre_4_bits registre_4_bits_4 (
    .Yi(registre_4_bits_4_yi), .Xi(registre_4_bits_4_xi), .R(select_4_s), .Wa(and_4_out), .Reset(Reset),
    .Preset(Preset), .rXi(and_8_out), .rYi(and_12_out), .clk(not_1_out), .Enable(Enable));
  Select select_12 (.R(registre_4_bits_4_xi), .enable(and_8_out), .S(select_12_s));
  Pull_Resistor pull_resistor_1 (.node(select_7_s));
  Pull_Resistor pull_resistor_2 (.node(select_5_s));
  Pull_Resistor pull_resistor_3 (.node(select_10_s));
  Pull_Resistor pull_resistor_4 (.node(select_6_s));
  Pull_Resistor pull_resistor_5 (.node(select_8_s));
  Pull_Resistor pull_resistor_6 (.node(select_9_s));
  Pull_Resistor pull_resistor_7 (.node(select_12_s));
  Pull_Resistor pull_resistor_8 (.node(select_11_s));
  assign Xi = select_5_s | select_7_s | select_9_s | select_12_s;  // OR_Gate or_1, 4 bits wide
  assign Yi = select_6_s | select_8_s | select_10_s | select_11_s;  // OR_Gate or_2, 4 bits wide
endmodule

module ALU_4_bits (
  input  SUBS,
  input  AND,
  input  OR,
  input  nB,
  input  ADD,
  input  Re,
  input  [3:0] A,
  input  [3:0] B,
  output [3:0] Res,
  output Rs,
  output Rs_subs
);

  wire alu_1_rs, alu_1_rs_subs, alu_2_rs, alu_2_rs_subs, alu_3_rs, alu_3_rs_subs;

  ALU alu_1 (
    .A(A[0]), .B(B[0]), .Re(Re), .S(Res[0]), .Rs(alu_1_rs), .AND(AND), .OR(OR), .nB(nB), .ADD(ADD),
    .Re_subs(1'b1), .SUBS(SUBS), .Rs_subs(alu_1_rs_subs));
  ALU alu_2 (
    .A(A[1]), .B(B[1]), .Re(alu_1_rs), .S(Res[1]), .Rs(alu_2_rs), .AND(AND), .OR(OR), .nB(nB), .ADD(ADD),
    .Re_subs(alu_1_rs_subs), .SUBS(SUBS), .Rs_subs(alu_2_rs_subs));
  ALU alu_3 (
    .A(A[2]), .B(B[2]), .Re(alu_2_rs), .S(Res[2]), .Rs(alu_3_rs), .AND(AND), .OR(OR), .nB(nB), .ADD(ADD),
    .Re_subs(alu_2_rs_subs), .SUBS(SUBS), .Rs_subs(alu_3_rs_subs));
  ALU alu_4 (
    .A(A[3]), .B(B[3]), .Re(alu_3_rs), .S(Res[3]), .Rs(Rs), .AND(AND), .OR(OR), .nB(nB), .ADD(ADD),
    .Re_subs(alu_3_rs_subs), .SUBS(SUBS), .Rs_subs(Rs_subs));
endmodule

module \Décodeur_d_instructions  (
  input  [11:0] Instruct_In,
  output SUBS,
  output ADD,
  output OR,
  output AND,
  output NOT,
  output LOAD,
  output STORE,
  output [1:0] Res,
  output [1:0] X,
  output [1:0] Y,
  output [5:0] Imme,
  output Read,
  output Write,
  output wAD,
  output Fetch,
  output wPC
);

  wire and_6_out, and_7_out, and_8_out, and_9_out, and_10_out, and_11_out, and_12_out, and_13_out,
       and_14_out, and_15_out, and_16_out, and_17_out;

  and u_SUBS (SUBS, Instruct_In[11], ~Instruct_In[10], ~Instruct_In[9], Instruct_In[8]);  // AND_Gate
  and u_ADD (ADD, ~Instruct_In[11], ~Instruct_In[10], ~Instruct_In[9], ~Instruct_In[8]);  // AND_Gate
  and u_OR (OR, ~Instruct_In[11], ~Instruct_In[10], ~Instruct_In[9], Instruct_In[8]);  // AND_Gate
  and u_AND (AND, ~Instruct_In[11], ~Instruct_In[10], Instruct_In[9], ~Instruct_In[8]);  // AND_Gate
  and u_NOT (NOT, ~Instruct_In[11], ~Instruct_In[10], Instruct_In[9], Instruct_In[8]);  // AND_Gate
  and u_LOAD (LOAD, ~Instruct_In[11], Instruct_In[10], ~Instruct_In[9], ~Instruct_In[8]);  // AND_Gate
  and u_STORE (STORE, Instruct_In[11], ~Instruct_In[10], ~Instruct_In[8], ~Instruct_In[8]);  // AND_Gate
  or or_2 (wAD, STORE, LOAD);
  and and_2 (X[0], ~STORE, ~LOAD, Instruct_In[4]);  // AND_Gate
  and and_3 (X[1], ~STORE, ~LOAD, Instruct_In[5]);  // AND_Gate
  and and_4 (Y[0], ~STORE, ~LOAD, Instruct_In[2]);  // AND_Gate
  and and_5 (Y[1], ~STORE, ~LOAD, Instruct_In[3]);  // AND_Gate
  and and_6 (and_6_out, Instruct_In[0], LOAD);
  and and_7 (and_7_out, Instruct_In[1], LOAD);
  and and_8 (and_8_out, Instruct_In[2], LOAD);
  and and_9 (and_9_out, Instruct_In[3], LOAD);
  and and_10 (and_10_out, Instruct_In[4], LOAD);
  and and_11 (and_11_out, Instruct_In[5], LOAD);
  and and_12 (and_12_out, Instruct_In[0], STORE);
  and and_13 (and_13_out, Instruct_In[1], STORE);
  and and_14 (and_14_out, Instruct_In[2], STORE);
  and and_15 (and_15_out, Instruct_In[3], STORE);
  and and_16 (and_16_out, Instruct_In[4], STORE);
  and and_17 (and_17_out, Instruct_In[5], STORE);
  or or_3 (Imme[0], and_12_out, and_6_out);
  or or_4 (Imme[1], and_13_out, and_7_out);
  or or_5 (Imme[2], and_14_out, and_8_out);
  or or_6 (Imme[3], and_15_out, and_9_out);
  or or_7 (Imme[4], and_16_out, and_10_out);
  or or_8 (Imme[5], and_17_out, and_11_out);

  assign Fetch = 1'b1;
  assign Read = LOAD;
  assign Res = Instruct_In[7:6];
  assign wPC = 1'b1;
  assign Write = STORE;
endmodule

module Registre_d_instructions (
  input  clk,
  input  [11:0] R,
  input  Winstrct,
  input  selXi,
  input  Reset,
  input  Enable,
  input  Preset,
  output [11:0] Xi
);

  wire controlled_buffer_1_out, controlled_buffer_2_out, controlled_buffer_3_out, controlled_buffer_4_out,
       controlled_buffer_5_out, controlled_buffer_6_out, controlled_buffer_7_out, controlled_buffer_8_out,
       controlled_buffer_9_out, controlled_buffer_10_out, controlled_buffer_11_out, controlled_buffer_12_out,
       d_ff_1_q, d_ff_2_q, d_ff_3_q, d_ff_4_q, d_ff_5_q, d_ff_6_q, d_ff_7_q, d_ff_8_q, d_ff_9_q, d_ff_10_q,
       d_ff_11_q, d_ff_12_q;

  assign controlled_buffer_1_out = Winstrct ? R[0] : 1'bz;  // Controlled_Buffer controlled_buffer_1
  assign controlled_buffer_2_out = Winstrct ? R[1] : 1'bz;  // Controlled_Buffer controlled_buffer_2
  assign controlled_buffer_3_out = Winstrct ? R[2] : 1'bz;  // Controlled_Buffer controlled_buffer_3
  assign controlled_buffer_4_out = Winstrct ? R[3] : 1'bz;  // Controlled_Buffer controlled_buffer_4
  assign controlled_buffer_5_out = Winstrct ? R[4] : 1'bz;  // Controlled_Buffer controlled_buffer_5
  assign controlled_buffer_6_out = Winstrct ? R[5] : 1'bz;  // Controlled_Buffer controlled_buffer_6
  assign controlled_buffer_7_out = Winstrct ? R[6] : 1'bz;  // Controlled_Buffer controlled_buffer_7
  assign controlled_buffer_8_out = Winstrct ? R[7] : 1'bz;  // Controlled_Buffer controlled_buffer_8
  assign controlled_buffer_9_out = Winstrct ? R[8] : 1'bz;  // Controlled_Buffer controlled_buffer_9
  assign controlled_buffer_10_out = Winstrct ? R[9] : 1'bz;  // Controlled_Buffer controlled_buffer_10
  assign controlled_buffer_11_out = Winstrct ? R[10] : 1'bz;  // Controlled_Buffer controlled_buffer_11
  assign controlled_buffer_12_out = Winstrct ? R[11] : 1'bz;  // Controlled_Buffer controlled_buffer_12
  D_Flip_Flop d_ff_1 (
    .clk(clk), .D(controlled_buffer_1_out), .Q(d_ff_1_q), .preset(Preset), .en(Enable), .reset(Reset));  // open: Qn
  D_Flip_Flop d_ff_2 (
    .clk(clk), .D(controlled_buffer_2_out), .Q(d_ff_2_q), .preset(Preset), .en(Enable), .reset(Reset));  // open: Qn
  D_Flip_Flop d_ff_3 (
    .clk(clk), .D(controlled_buffer_3_out), .Q(d_ff_3_q), .preset(Preset), .en(Enable), .reset(Reset));  // open: Qn
  D_Flip_Flop d_ff_4 (
    .clk(clk), .D(controlled_buffer_4_out), .Q(d_ff_4_q), .preset(Preset), .en(Enable), .reset(Reset));  // open: Qn
  D_Flip_Flop d_ff_5 (
    .clk(clk), .D(controlled_buffer_5_out), .Q(d_ff_5_q), .preset(Preset), .en(Enable), .reset(Reset));  // open: Qn
  D_Flip_Flop d_ff_6 (
    .clk(clk), .D(controlled_buffer_6_out), .Q(d_ff_6_q), .preset(Preset), .en(Enable), .reset(Reset));  // open: Qn
  D_Flip_Flop d_ff_7 (
    .clk(clk), .D(controlled_buffer_7_out), .Q(d_ff_7_q), .preset(Preset), .en(Enable), .reset(Reset));  // open: Qn
  D_Flip_Flop d_ff_8 (
    .clk(clk), .D(controlled_buffer_8_out), .Q(d_ff_8_q), .preset(Preset), .en(Enable), .reset(Reset));  // open: Qn
  D_Flip_Flop d_ff_9 (
    .clk(clk), .D(controlled_buffer_9_out), .Q(d_ff_9_q), .preset(Preset), .en(Enable), .reset(Reset));  // open: Qn
  D_Flip_Flop d_ff_10 (
    .clk(clk), .D(controlled_buffer_10_out), .Q(d_ff_10_q), .preset(Preset), .en(Enable), .reset(Reset));  // open: Qn
  D_Flip_Flop d_ff_11 (
    .clk(clk), .D(controlled_buffer_11_out), .Q(d_ff_11_q), .preset(Preset), .en(Enable), .reset(Reset));  // open: Qn
  D_Flip_Flop d_ff_12 (
    .clk(clk), .D(controlled_buffer_12_out), .Q(d_ff_12_q), .preset(Preset), .en(Enable), .reset(Reset));  // open: Qn
  assign Xi[0] = selXi ? d_ff_1_q : 1'bz;  // Controlled_Buffer controlled_buffer_13
  assign Xi[1] = selXi ? d_ff_2_q : 1'bz;  // Controlled_Buffer controlled_buffer_14
  assign Xi[2] = selXi ? d_ff_3_q : 1'bz;  // Controlled_Buffer controlled_buffer_15
  assign Xi[3] = selXi ? d_ff_4_q : 1'bz;  // Controlled_Buffer controlled_buffer_16
  assign Xi[4] = selXi ? d_ff_5_q : 1'bz;  // Controlled_Buffer controlled_buffer_17
  assign Xi[5] = selXi ? d_ff_6_q : 1'bz;  // Controlled_Buffer controlled_buffer_18
  assign Xi[6] = selXi ? d_ff_7_q : 1'bz;  // Controlled_Buffer controlled_buffer_19
  assign Xi[7] = selXi ? d_ff_8_q : 1'bz;  // Controlled_Buffer controlled_buffer_20
  assign Xi[8] = selXi ? d_ff_9_q : 1'bz;  // Controlled_Buffer controlled_buffer_21
  assign Xi[9] = selXi ? d_ff_10_q : 1'bz;  // Controlled_Buffer controlled_buffer_22
  assign Xi[10] = selXi ? d_ff_11_q : 1'bz;  // Controlled_Buffer controlled_buffer_23
  assign Xi[11] = selXi ? d_ff_12_q : 1'bz;  // Controlled_Buffer controlled_buffer_24
endmodule

module Controleur (
  input  clk,
  input  [11:0] Instruct_In,
  output SUBS,
  output ADD,
  output OR,
  output AND,
  output NOT,
  output LOAD,
  output wPC,
  output STORE,
  output [1:0] X,
  output wAD,
  output Write,
  output [1:0] Y,
  output Read,
  output Fetch,
  output [5:0] Imme,
  output [1:0] Res
);

  wire and_21_out, and_22_out, and_23_out, and_24_out, \décodeur_d_instructions_1_add ,
       \décodeur_d_instructions_1_and , \décodeur_d_instructions_1_fetch , \décodeur_d_instructions_1_load ,
       \décodeur_d_instructions_1_not , \décodeur_d_instructions_1_or , \décodeur_d_instructions_1_store ,
       \décodeur_d_instructions_1_subs , \décodeur_d_instructions_1_wad , \décodeur_d_instructions_1_wpc ,
       or_1_out, \registe_à_décalage_1_s1 , \registe_à_décalage_1_s2 , \registe_à_décalage_1_s3 ,
       \registe_à_décalage_1_s4 ;
  wire [1:0] \décodeur_d_instructions_1_res , \décodeur_d_instructions_1_x , \décodeur_d_instructions_1_y ;
  wire [5:0] \décodeur_d_instructions_1_imme ;

  \Décodeur_d_instructions  \décodeur_d_instructions_1  (
    .ADD(\décodeur_d_instructions_1_add ), .OR(\décodeur_d_instructions_1_or ),
    .AND(\décodeur_d_instructions_1_and ), .NOT(\décodeur_d_instructions_1_not ),
    .LOAD(\décodeur_d_instructions_1_load ), .STORE(\décodeur_d_instructions_1_store ),
    .Res(\décodeur_d_instructions_1_res ), .X(\décodeur_d_instructions_1_x ), .Read(Read), .Write(Write),
    .wAD(\décodeur_d_instructions_1_wad ), .Fetch(\décodeur_d_instructions_1_fetch ),
    .wPC(\décodeur_d_instructions_1_wpc ), .Instruct_In(Instruct_In), .Y(\décodeur_d_instructions_1_y ),
    .Imme(\décodeur_d_instructions_1_imme ), .SUBS(\décodeur_d_instructions_1_subs ));
  and and_1 (wPC, \décodeur_d_instructions_1_wpc , \registe_à_décalage_1_s1 );
  and and_2 (wAD, \décodeur_d_instructions_1_wad , \registe_à_décalage_1_s3 );
  and and_3 (Fetch, \décodeur_d_instructions_1_fetch , ~\registe_à_décalage_1_s4 , ~\registe_à_décalage_1_s3 , ~\registe_à_décalage_1_s2 , \registe_à_décalage_1_s1 );  // AND_Gate
  \Registe_à_décalage  \registe_à_décalage_1  (
    .clk(clk), .S1(\registe_à_décalage_1_s1 ), .S2(\registe_à_décalage_1_s2 ),
    .S3(\registe_à_décalage_1_s3 ), .S4(\registe_à_décalage_1_s4 ));
  or or_1 (or_1_out, \décodeur_d_instructions_1_load , \décodeur_d_instructions_1_store );
  and and_4 (SUBS, \décodeur_d_instructions_1_subs , \registe_à_décalage_1_s2 );
  and and_5 (ADD, \décodeur_d_instructions_1_add , \registe_à_décalage_1_s2 );
  and and_6 (OR, \décodeur_d_instructions_1_or , \registe_à_décalage_1_s2 );
  and and_7 (AND, \décodeur_d_instructions_1_and , \registe_à_décalage_1_s2 );
  and and_8 (NOT, \décodeur_d_instructions_1_not , \registe_à_décalage_1_s2 );
  and and_9 (LOAD, \décodeur_d_instructions_1_load , \registe_à_décalage_1_s2 );
  and and_10 (STORE, \décodeur_d_instructions_1_store , \registe_à_décalage_1_s2 );
  and and_11 (Y[0], \décodeur_d_instructions_1_y [0], \registe_à_décalage_1_s3 );
  and and_12 (Y[1], \décodeur_d_instructions_1_y [1], \registe_à_décalage_1_s3 );
  and and_13 (Res[0], \décodeur_d_instructions_1_res [0], ~\décodeur_d_instructions_1_store , \registe_à_décalage_1_s3 );  // AND_Gate
  and and_14 (Res[1], \décodeur_d_instructions_1_res [1], ~\décodeur_d_instructions_1_store , \registe_à_décalage_1_s3 );  // AND_Gate
  and and_15 (Imme[0], \décodeur_d_instructions_1_imme [0], or_1_out, \registe_à_décalage_1_s3 );
  and and_16 (Imme[1], \décodeur_d_instructions_1_imme [1], or_1_out, \registe_à_décalage_1_s3 );
  and and_17 (Imme[2], \décodeur_d_instructions_1_imme [2], or_1_out, \registe_à_décalage_1_s3 );
  and and_18 (Imme[3], \décodeur_d_instructions_1_imme [3], or_1_out, \registe_à_décalage_1_s3 );
  and and_19 (Imme[4], \décodeur_d_instructions_1_imme [4], or_1_out, \registe_à_décalage_1_s3 );
  and and_20 (Imme[5], \décodeur_d_instructions_1_imme [5], or_1_out, \registe_à_décalage_1_s3 );
  and and_21 (and_21_out, \décodeur_d_instructions_1_x [0], ~\décodeur_d_instructions_1_store , \registe_à_décalage_1_s3 );  // AND_Gate
  and and_22 (and_22_out, \décodeur_d_instructions_1_x [1], ~\décodeur_d_instructions_1_store , \registe_à_décalage_1_s3 );  // AND_Gate
  and and_23 (and_23_out, \décodeur_d_instructions_1_store , \décodeur_d_instructions_1_res [0]);
  and and_24 (and_24_out, \décodeur_d_instructions_1_store , \décodeur_d_instructions_1_res [1]);
  or or_2 (X[0], and_21_out, and_23_out);
  or or_3 (X[1], and_22_out, and_24_out);
endmodule

module \Registe_à_décalage  (
  input  clk,
  output S1,
  output S2,
  output S3,
  output S4
);

  wire and_1_out;

  D_Flip_Flop d_ff_1 (.clk(clk), .D(1'b1), .Q(S1), .preset(1'b0), .en(1'b1), .reset(and_1_out));  // open: Qn
  D_Flip_Flop d_ff_2 (.clk(clk), .D(S1), .Q(S2), .preset(1'b0), .en(1'b1), .reset(and_1_out));  // open: Qn
  D_Flip_Flop d_ff_3 (.clk(clk), .D(S2), .Q(S3), .preset(1'b0), .en(1'b1), .reset(and_1_out));  // open: Qn
  D_Flip_Flop d_ff_4 (.clk(clk), .D(S3), .Q(S4), .preset(1'b0), .en(1'b1), .reset(and_1_out));  // open: Qn
  and and_1 (and_1_out, ~clk, S1, S2, S3, S4);  // AND_Gate
endmodule

module PC (
  input  Preset,
  input  Reset,
  input  clk,
  input  [3:0] \Entrée_PC ,
  input  read_PC,
  input  increment,
  input  write_PC,
  output [3:0] S_PC
);

  wire not_1_out, or_1_out, or_2_out, xor_1_out;
  wire [3:0] alu_4_bits_1_res, or_3_out, select_1_s, select_2_s;

  xor xor_1 (xor_1_out, ~increment, write_PC);  // XOR_Gate
  not not_1 (not_1_out, increment);
  or or_1 (or_1_out, read_PC, increment);
  or or_2 (or_2_out, write_PC, increment);
  Select select_1 (.R(\Entrée_PC ), .enable(not_1_out), .S(select_1_s));
  Pull_Resistor pull_resistor_1 (.node(select_1_s));
  Select select_2 (.R(alu_4_bits_1_res), .enable(increment), .S(select_2_s));
  Pull_Resistor pull_resistor_2 (.node(select_2_s));
  assign or_3_out = select_1_s | select_2_s;  // OR_Gate or_3, 4 bits wide
  Registre_4_bits registre_4_bits_1 (
    .Xi(S_PC), .R(or_3_out), .Wa(or_2_out), .Reset(Reset), .Preset(Preset), .rXi(or_1_out), .rYi(1'b0),
    .clk(clk), .Enable(xor_1_out));  // open: Yi
  Pull_Resistor pull_resistor_3 (.node(S_PC));
  ALU_4_bits alu_4_bits_1 (
    .Re(1'b0), .A(4'b0001), .B(S_PC), .AND(1'b0), .OR(1'b0), .nB(1'b0), .ADD(1'b1), .Res(alu_4_bits_1_res),
    .SUBS(1'b0));  // open: Rs, Rs_subs
endmodule

module AD (
  input  clk,
  input  [5:0] R,
  input  Reset,
  input  Wa,
  input  Enable,
  input  Preset,
  output [5:0] R_2
);

  wire controlled_buffer_1_out, controlled_buffer_2_out, controlled_buffer_3_out, controlled_buffer_4_out,
       controlled_buffer_5_out, controlled_buffer_6_out, not_1_out;

  assign controlled_buffer_1_out = Wa ? R[0] : 1'bz;  // Controlled_Buffer controlled_buffer_1
  assign controlled_buffer_2_out = Wa ? R[1] : 1'bz;  // Controlled_Buffer controlled_buffer_2
  assign controlled_buffer_3_out = Wa ? R[2] : 1'bz;  // Controlled_Buffer controlled_buffer_3
  assign controlled_buffer_4_out = Wa ? R[3] : 1'bz;  // Controlled_Buffer controlled_buffer_4
  assign controlled_buffer_5_out = Wa ? R[4] : 1'bz;  // Controlled_Buffer controlled_buffer_5
  assign controlled_buffer_6_out = Wa ? R[5] : 1'bz;  // Controlled_Buffer controlled_buffer_6
  not not_1 (not_1_out, clk);
  D_Flip_Flop d_ff_1 (
    .clk(not_1_out), .D(controlled_buffer_1_out), .Q(R_2[0]), .preset(Preset), .en(Enable), .reset(Reset));  // open: Qn
  D_Flip_Flop d_ff_2 (
    .clk(not_1_out), .D(controlled_buffer_2_out), .Q(R_2[1]), .preset(Preset), .en(Enable), .reset(Reset));  // open: Qn
  D_Flip_Flop d_ff_3 (
    .clk(not_1_out), .D(controlled_buffer_3_out), .Q(R_2[2]), .preset(Preset), .en(Enable), .reset(Reset));  // open: Qn
  D_Flip_Flop d_ff_4 (
    .clk(not_1_out), .D(controlled_buffer_4_out), .Q(R_2[3]), .preset(Preset), .en(Enable), .reset(Reset));  // open: Qn
  D_Flip_Flop d_ff_5 (
    .clk(not_1_out), .D(controlled_buffer_5_out), .Q(R_2[4]), .preset(Preset), .en(Enable), .reset(Reset));  // open: Qn
  D_Flip_Flop d_ff_6 (
    .clk(not_1_out), .D(controlled_buffer_6_out), .Q(R_2[5]), .preset(Preset), .en(Enable), .reset(Reset));  // open: Qn
endmodule

module Substractor (
  input  A,
  input  B,
  input  Re,
  output Rs,
  output S
);

  wire and_1_out, and_2_out, and_3_out, not_1_out, xor_1_out;

  not not_1 (not_1_out, B);
  and and_1 (and_1_out, A, Re);
  and and_2 (and_2_out, not_1_out, Re);
  and and_3 (and_3_out, not_1_out, A);
  or or_1 (Rs, and_1_out, and_2_out, and_3_out);
  xor xor_1 (xor_1_out, Re, not_1_out);
  xor xor_2 (S, xor_1_out, A);
endmodule
